// Logisim project Group_B2_6_Problem_2.circ as structural Verilog: 1 circuit, main circuit main
module main (
  input  A,
  input  B,
  input  C,
  output X,
  output Y,
  output Z
);

  wire AND_p3, AND_p6, AND_p11, AND_p14, n7408_1_p3, n7408_1_p7, n7408_2_p4, n7408_2_p7, n7408_2_p12,
       n7408_2_p15, NOT_p2, NOT_p4, NOT_p8, OR_p3, OR_p6;

  // _7404 NOT: pin names not known; wires that end beside it: A, NOT_p2, B, NOT_p4, 1'b0, 1'b1, C, NOT_p8
  // _7408 7408_1: pin names not known; wires that end beside it: NOT_p2, B, n7408_1_p3, 1'b1, A, NOT_p4, n7408_1_p7
  // _7408 7408_2: pin names not known; wires that end beside it: 1'b0, A, NOT_p4, n7408_2_p4, n7408_2_p4, NOT_p8, n7408_2_p7, 1'b0, 1'b1, A, B, n7408_2_p12, n7408_2_p12, C, n7408_2_p15
  // _7408 AND: pin names not known; wires that end beside it: NOT_p2, NOT_p4, AND_p3, AND_p3, C, AND_p6, 1'b0, 1'b1, NOT_p2, B, AND_p11, AND_p11, NOT_p8, AND_p14
  // _7432 OR: pin names not known; wires that end beside it: AND_p6, AND_p14, OR_p3, OR_p3, n7408_2_p7, OR_p6, 1'b0, 1'b1, OR_p6, n7408_2_p15, Z, n7408_1_p3, n7408_1_p7, Y

  assign X = A;
endmodule
