// Logisim project Group_B2_6_Problem_3.circ as structural Verilog: 1 circuit, main circuit main
module main (
  input  A,
  input  C,
  input  B,
  output LED_1,
  output LED_0
);

  wire n7408_1_p3, n7408_1_p8, n7408_1_p11, n7408_2_p2, n7408_2_p3, n7408_2_p4, n7408_2_p5, n7408_2_p8,
       n7408_2_p9, n7408_2_p10, n7408_2_p12, n7408_2_p13, n7432_1_p8;

  // _7408 7408_1: pin names not known; wires that end beside it: A, B, n7408_1_p3, 1'b0, 1'b1, C, B, n7408_1_p8, C, A, n7408_1_p11
  // _7408 7408_2: pin names not known; wires that end beside it: 1'b0, n7408_2_p2, n7408_2_p3, n7408_2_p4, n7408_2_p5, C, A, n7408_2_p8, n7408_2_p9, n7408_2_p10, B, n7408_2_p12, n7408_2_p13, 1'b1
  // _7404 7404_1: pin names not known; wires that end beside it: A, n7408_2_p13, B, n7408_2_p5, 1'b0, 1'b1, C, n7408_2_p12, n7408_2_p10, n7408_2_p4
  // _7432 7432_1: pin names not known; wires that end beside it: 1'b0, LED_0, n7408_2_p10, n7408_2_p8, n7408_2_p3, n7408_2_p2, n7408_2_p9, n7432_1_p8, LED_1, n7408_1_p11, n7432_1_p8, n7408_1_p3, n7408_1_p8, 1'b1
endmodule
