// Logisim project 1805116_offline3_qs2.circ as structural Verilog: 1 circuit, main circuit main
module main (
  input  SHIFT_RIGHT,
  input  SHIFT_LEFT,
  input  S1,
  input  S0,
  input  I3,
  input  I2,
  input  I1,
  input  I0,
  output O3,
  output O2,
  output O1,
  output O0
);

  wire _4_1_MUX_2_p7, _4_1_MUX_2_p14, _4_1_MUX_p7, _4_1_MUX_p14, CLOCK_out, D_Flip_Flop_p1;

  // _74153 _4_1_MUX: pin names not known; wires that end beside it: 1'b0, S1, I3, O2, SHIFT_RIGHT, O3, _4_1_MUX_p7, 1'b0, S0, I2, O1, O3, O2, _4_1_MUX_p14
  // _74153 _4_1_MUX_2: pin names not known; wires that end beside it: 1'b0, S1, I1, O0, O2, O1, _4_1_MUX_2_p7, 1'b0, S0, I0, SHIFT_LEFT, O1, O0, _4_1_MUX_2_p14
  Clock CLOCK (.out(CLOCK_out));
  // _7474 D_Flip_Flop: pin names not known; wires that end beside it: D_Flip_Flop_p1, _4_1_MUX_p7, CLOCK_out, O3, D_Flip_Flop_p1, _4_1_MUX_p14, CLOCK_out, O2
  // _7474 D_Flip_Flop_2: pin names not known; wires that end beside it: D_Flip_Flop_p1, _4_1_MUX_2_p7, CLOCK_out, O1, D_Flip_Flop_p1, _4_1_MUX_2_p14, CLOCK_out, O0
  Button CLEAR (.out(D_Flip_Flop_p1));
endmodule
