// Logisim project Group_B2_6_Problem 1.circ as structural Verilog: 1 circuit, main circuit main
module main (
  input  PRESET,
  input  J,
  input  K,
  input  CLEAR,
  output Q,
  output Q_prime
);

  wire clock_1_out, n7400_1_p3, n7400_1_p6, n7400_1_p8, n7400_1_p9, n7400_2_p3, n7400_2_p6, n7400_2_p8,
       n7400_2_p9, n7400_3_p3, n7400_3_p6, n7400_3_p8, n7400_3_p9, n7400_4_p1, n7400_4_p3, n7400_4_p6;

  Clock clock_1 (.out(clock_1_out));
  // _7400 7400_1: pin names not known; wires that end beside it: J, clock_1_out, n7400_1_p3, n7400_1_p3, n7400_1_p3, n7400_1_p6, PRESET, n7400_1_p8, n7400_1_p9, Q_prime, n7400_1_p6, n7400_1_p8
  // _7400 7400_2: pin names not known; wires that end beside it: clock_1_out, K, n7400_2_p3, n7400_2_p3, n7400_2_p3, n7400_2_p6, CLEAR, n7400_2_p8, n7400_2_p9, Q, n7400_2_p6, n7400_2_p8
  // _7400 7400_3: pin names not known; wires that end beside it: n7400_1_p9, n7400_1_p9, n7400_3_p3, n7400_2_p9, n7400_2_p9, n7400_3_p6, n7400_3_p3, n7400_3_p8, n7400_3_p9, n7400_3_p6, n7400_3_p9, n7400_3_p8
  // _7400 7400_4: pin names not known; wires that end beside it: n7400_4_p1, n7400_3_p9, n7400_4_p3, n7400_3_p8, n7400_4_p1, n7400_4_p6, n7400_4_p3, Q_prime, Q, clock_1_out, clock_1_out, n7400_4_p1
  // _7400 7400_5: pin names not known; wires that end beside it: Q, n7400_4_p6, Q_prime
endmodule
