// Logisim project Online2_2_1805117.circ as structural Verilog: 1 circuit, main circuit main
module main (
  input  P,
  input  Q,
  input  R,
  input  S,
  output f
);

  wire n7404_1_p2, n7404_1_p4, n7404_1_p8, n7404_1_p10, n7408_1_p3, n7408_1_p6, n7408_1_p11, n7408_1_p14,
       n7432_1_p3;

  // _7404 7404_1: pin names not known; wires that end beside it: P, n7404_1_p2, Q, n7404_1_p4, 1'b0, 1'b1, R, n7404_1_p8, S, n7404_1_p10
  // _7408 7408_1: pin names not known; wires that end beside it: P, Q, n7408_1_p3, R, n7404_1_p10, n7408_1_p6, 1'b0, 1'b1, n7404_1_p2, n7404_1_p4, n7408_1_p11, n7408_1_p11, n7404_1_p8, n7408_1_p14
  // _7432 7432_1: pin names not known; wires that end beside it: n7408_1_p14, n7408_1_p3, n7432_1_p3, n7432_1_p3, n7408_1_p6, f, 1'b0, 1'b1
endmodule
