// Logisim project 1805117.circ as structural Verilog: 1 circuit, main circuit main
module main (
  input  in_1,
  input  A,
  input  B,
  input  C,
  input  in_5,
  input  in_6,
  input  D,
  input  in_8,
  input  in_9,
  input  in_10,
  output f
);

  wire n74151_1_p3;

  // _74151 74151_1: pin names not known; wires that end beside it: in_6, D, n74151_1_p3, in_9, f, 1'b0, 1'b0, 1'b1, in_5, D, D, in_1, C, B, A
  // _74157 74157_1: pin names not known; wires that end beside it: D, 1'b0, 1'b1, 1'b0, in_8, in_10, n74151_1_p3
endmodule
