// Logisim project 1805117.circ as structural Verilog: 1 circuit, main circuit main
module main (
  input  in_1,
  output y2,
  output y1,
  output y0
);

  wire clock_1_out, n7408_1_p2, n7408_1_p3, n7408_1_p4, n7408_1_p6, n7408_1_p11, n7476_1_p2, n7476_1_p5,
       n7476_1_p12, n7476_2_p2;

  Clock clock_1 (.out(clock_1_out));
  // _7408 7408_1: pin names not known; wires that end beside it: y0, n7408_1_p2, n7408_1_p3, n7408_1_p4, y1, n7408_1_p6, 1'b0, 1'b1, y0, y2, n7408_1_p11
  // _7476 7476_1: pin names not known; wires that end beside it: clock_1_out, n7476_1_p2, 1'b1, clock_1_out, n7476_1_p5, y0, n7408_1_p4, 1'b0, n7408_1_p11, y1, n7408_1_p2, n7476_1_p12
  // _7476 7476_2: pin names not known; wires that end beside it: clock_1_out, n7476_2_p2, 1'b1, in_1, y2, n7476_1_p2, 1'b0
  // _7432 7432_1: pin names not known; wires that end beside it: n7408_1_p3, n7408_1_p6, n7476_2_p2, y0, y2, n7476_1_p12, 1'b0, 1'b1, n7476_1_p2, n7408_1_p2, n7476_1_p5
endmodule
