// Logisim project 1805117.circ as structural Verilog: 1 circuit, main circuit main
module main (
  input  X1,
  input  X2,
  output Z1,
  output Z2,
  output Y1,
  output Y2
);

  wire button_1_out, n7404_1_p2, n7408_1_p2, n7408_1_p3, n7408_1_p4, n7408_1_p6, n7408_1_p11, n7408_2_p3,
       n7408_2_p6, n7408_2_p11, n7408_2_p14, n7408_3_p6, n7408_4_p3, n7432_1_p3, n7432_1_p11, n7432_2_p9,
       n7432_2_p12, n7474_1_p8, n7476_1_p1, n7476_1_p3, n7476_1_p7, n7476_1_p9, n7476_1_p13;

  Button button_1 (.out(button_1_out));
  // _7408 7408_1: pin names not known; wires that end beside it: X1, n7408_1_p2, n7408_1_p3, n7408_1_p4, X2, n7408_1_p6, 1'b0, 1'b1, Y1, X1, n7408_1_p11, Y1, Y2, n7408_1_p4
  // _7404 7404_1: pin names not known; wires that end beside it: X1, n7404_1_p2, X2, n7408_1_p2, 1'b1
  // _7476 7476_1: pin names not known; wires that end beside it: n7476_1_p1, button_1_out, n7476_1_p3, 1'b1, n7476_1_p1, button_1_out, n7476_1_p7, Y1, n7476_1_p9, 1'b0, n7404_1_p2, Y2, n7476_1_p13
  // _7408 7408_2: pin names not known; wires that end beside it: X1, X2, n7408_2_p3, n7404_1_p2, n7408_1_p2, n7408_2_p6, 1'b0, 1'b1, Y2, X2, n7408_2_p11, Y2, X2, n7408_2_p14
  // _7408 7408_3: pin names not known; wires that end beside it: X1, n7408_1_p2, n7476_1_p3, 1'b0, 1'b1, n7408_3_p6, X2, n7476_1_p13
  // _7432 7432_1: pin names not known; wires that end beside it: n7408_2_p3, n7408_2_p6, n7432_1_p3, n7432_1_p3, n7408_2_p11, n7476_1_p7, 1'b0, 1'b1, Y1, Y2, n7432_1_p11
  // _7432 7432_2: pin names not known; wires that end beside it: n7404_1_p2, n7476_1_p9, n7408_3_p6, n7408_2_p14, 1'b0, 1'b1, n7408_1_p3, n7408_1_p11, n7432_2_p9, n7432_2_p9, n7408_1_p6, n7432_2_p12
  // _7474 7474_1: pin names not known; wires that end beside it: button_1_out, n7432_2_p12, n7476_1_p1, Z1, 1'b0, 1'b1, button_1_out, n7474_1_p8, n7476_1_p1, Z2
  // _7408 7408_4: pin names not known; wires that end beside it: n7432_1_p11, n7404_1_p2, n7408_4_p3, 1'b0, 1'b1, n7408_4_p3, n7408_1_p2, n7474_1_p8
  Clock clock_1 (.out(n7476_1_p1));
endmodule
