// Logisim project OnlineA1_B1_Vending.circ as structural Verilog: 1 circuit, main circuit main
module main (
  input  X1,
  input  X2,
  output Z1,
  output Z2,
  output Y1,
  output Y2
);

  wire button_1_out, clock_1_out, n7404_1_p2, n7404_1_p4, n7408_1_p3, n7408_1_p6, n7408_1_p9, n7408_1_p12,
       n7408_2_p3, n7408_2_p6, n7408_2_p9, n7408_2_p10, n7408_2_p12, n7408_3_p10, n7408_4_p3, n7408_5_p3,
       n7408_5_p9, n7432_1_p3, n7432_2_p3, n7432_2_p6, n7432_2_p7, n7432_2_p8, n7432_2_p9, n7432_2_p10,
       n7432_2_p11, n7432_3_p1, n7432_3_p2, n7432_3_p4, n7432_3_p5, n7432_3_p7, n7432_3_p8, n7474_1_p2,
       n7474_1_p7, n7474_1_p10;

  Clock clock_1 (.out(clock_1_out));
  Button button_1 (.out(button_1_out));
  // _7432 7432_1: pin names not known; wires that end beside it: Y1, Y2, n7432_1_p3
  // _7404 7404_1: pin names not known; wires that end beside it: X1, n7404_1_p2, X2, n7404_1_p4
  // _7408 7408_1: pin names not known; wires that end beside it: n7404_1_p4, X1, n7408_1_p3, n7408_1_p3, n7432_1_p3, n7408_1_p6, X1, X1, n7408_1_p9, n7404_1_p4, n7404_1_p2, n7408_1_p12
  // _7408 7408_2: pin names not known; wires that end beside it: Y1, Y2, n7408_2_p3, n7408_2_p3, X2, n7408_2_p6, n7408_1_p12, Y1, n7408_2_p9, n7408_2_p10, n7404_1_p2, n7408_2_p12
  // _7474 7474_1: pin names not known; wires that end beside it: button_1_out, n7474_1_p2, clock_1_out, Y1, n7408_2_p10, button_1_out, n7474_1_p7, clock_1_out, Y2, n7474_1_p10
  // _7432 7432_2: pin names not known; wires that end beside it: n7408_1_p9, n7408_2_p9, n7432_2_p3, n7432_2_p3, n7408_2_p6, n7432_2_p6, n7432_2_p7, n7432_2_p8, n7432_2_p9, n7432_2_p10, n7432_2_p11, n7474_1_p7
  // _7432 7432_3: pin names not known; wires that end beside it: n7432_3_p1, n7432_3_p2, n7474_1_p2, n7432_3_p4, n7432_3_p5, n7432_3_p1, n7432_3_p7, n7432_3_p8, n7432_3_p4
  // _7474 7474_2: pin names not known; wires that end beside it: button_1_out, n7408_1_p6, clock_1_out, Z2, button_1_out, n7432_2_p6, clock_1_out, Z1
  // _7408 7408_3: pin names not known; wires that end beside it: n7404_1_p4, n7404_1_p2, n7432_2_p7, n7432_2_p9, Y2, n7432_2_p10, X1, X2, n7432_2_p8, n7408_3_p10, n7404_1_p2, n7432_3_p7
  // _7408 7408_4: pin names not known; wires that end beside it: n7474_1_p10, n7404_1_p2, n7408_4_p3, n7408_4_p3, X2, n7432_2_p11, n7404_1_p4, n7408_2_p12, n7432_3_p8, n7408_2_p10, Y2, n7408_3_p10
  // _7408 7408_5: pin names not known; wires that end beside it: Y1, X1, n7408_5_p3, n7408_5_p3, X2, n7432_3_p2, Y1, n7474_1_p10, n7408_5_p9, n7408_5_p9, X2, n7432_3_p5
endmodule
