// Logisim project X-OR gate.circ as structural Verilog: 2 circuits, main circuit main
module main (
  input  A,
  input  B,
  output out_3
);

  wire and_1_out, and_2_out, not_1_out, not_2_out;

  not not_1 (not_1_out, A);
  not not_2 (not_2_out, B);
  and and_1 (and_1_out, not_1_out, B);
  and and_2 (and_2_out, A, not_2_out);
  or or_1 (out_3, and_1_out, and_2_out);
endmodule

module Practice1 (
  input  B,
  input  C,
  input  A,
  output out_4
);

  wire n7404_1_p6, n7408_1_p3, n7408_1_p6, n7408_1_p7;

  // _7408 7408_1: pin names not known; wires that end beside it: A, C, n7408_1_p3, 1'b0, 1'b1, n7408_1_p6, n7408_1_p7, out_4
  // _7404 7404_1: pin names not known; wires that end beside it: n7408_1_p3, n7408_1_p7, 1'b0, 1'b1, A, n7404_1_p6
  // _7432 7432_1: pin names not known; wires that end beside it: n7404_1_p6, B, n7408_1_p6, 1'b0, 1'b1
endmodule
