// Logisim project Group_B2_6_Problem_1.circ as structural Verilog: 1 circuit, main circuit main
module main (
  input  A,
  input  B,
  input  C,
  input  D,
  output F
);

  wire n7404_1_p2, n7404_1_p7, n7408_1_p3, n7408_1_p6;

  // _7404 7404_1: pin names not known; wires that end beside it: B, n7404_1_p2, 1'b0, A, 1'b1, D, n7404_1_p7
  // _7408 7408_1: pin names not known; wires that end beside it: n7404_1_p2, n7404_1_p7, n7408_1_p3, B, D, n7408_1_p6, 1'b0, 1'b1, C
  // _7432 7432_1: pin names not known; wires that end beside it: n7408_1_p3, n7408_1_p6, F, 1'b0, 1'b1
endmodule
