// Logisim project Group_B2_6_Problem_4.circ as structural Verilog: 1 circuit, main circuit main
module main (
  input  A,
  input  B,
  input  C,
  input  D,
  output out_5
);

  wire n7404_1_p2, n7404_1_p4, n7404_1_p6, n7404_1_p10, n7408_1_p3, n7408_1_p6, n7408_1_p11, n7408_1_p13,
       n7408_1_p14, n7408_2_p3, n7408_2_p6, n7408_2_p9, n7408_2_p10, n7408_2_p11;

  // _7404 7404_1: pin names not known; wires that end beside it: A, n7404_1_p2, B, n7404_1_p4, C, n7404_1_p6, 1'b0, 1'b1, D, n7404_1_p10
  // _7408 7408_1: pin names not known; wires that end beside it: n7404_1_p4, D, n7408_1_p3, B, n7404_1_p10, n7408_1_p6, 1'b0, 1'b1, A, n7404_1_p6, n7408_1_p11, n7408_1_p11, n7408_1_p13, n7408_1_p14
  // _7408 7408_2: pin names not known; wires that end beside it: n7404_1_p2, n7404_1_p10, n7408_2_p3, A, D, n7408_2_p6, 1'b0, 1'b1, n7408_2_p9, n7408_2_p10, n7408_2_p11, B, C, n7408_2_p10
  // _7432 7432_1: pin names not known; wires that end beside it: n7408_1_p3, n7408_1_p6, n7408_1_p13, n7408_2_p3, n7408_2_p6, n7408_2_p9, 1'b0, 1'b1, n7408_1_p14, n7408_2_p11, out_5
endmodule
