// Logisim project Group_B2_6_Problem_1.circ as structural Verilog: 1 circuit, main circuit main
module main (
  input  P1,
  input  P0,
  input  Q1,
  input  Q0,
  output A,
  output B,
  output C
);

  wire n7404_1_p2, n7404_1_p4, n7404_1_p8, n7404_1_p10, n7404_2_p2, n7404_2_p4, n7408_1_p3, n7408_1_p6,
       n7408_1_p10, n7408_1_p11, n7408_2_p3, n7408_2_p6, n7408_2_p10, n7408_2_p11, n7486_1_p3, n7486_1_p6;

  // _7404 7404_1: pin names not known; wires that end beside it: P1, n7404_1_p2, P0, n7404_1_p4, 1'b0, 1'b1, Q1, n7404_1_p8, Q0, n7404_1_p10
  // _7486 7486_1: pin names not known; wires that end beside it: P0, Q0, n7486_1_p3, P1, Q1, n7486_1_p6, 1'b0, 1'b1
  // _7408 7408_1: pin names not known; wires that end beside it: n7404_1_p2, Q1, n7408_1_p3, n7404_1_p4, Q0, n7408_1_p6, 1'b0, 1'b1, n7408_1_p6, n7408_1_p10, n7408_1_p11
  // _7404 7404_2: pin names not known; wires that end beside it: n7486_1_p3, n7404_2_p2, n7486_1_p6, n7404_2_p4, 1'b0, 1'b1
  // _7408 7408_2: pin names not known; wires that end beside it: P1, n7404_1_p8, n7408_2_p3, P0, n7404_1_p10, n7408_2_p6, 1'b0, 1'b1, n7408_2_p6, n7408_2_p10, n7408_2_p11, n7404_2_p2, n7404_2_p4, B
  // _7432 7432_1: pin names not known; wires that end beside it: n7408_2_p3, n7408_2_p11, A, P1, n7404_1_p8, n7408_2_p10, 1'b0, 1'b1
  // _7432 7432_2: pin names not known; wires that end beside it: n7408_1_p3, n7408_1_p11, C, n7404_1_p2, Q1, n7408_1_p10, 1'b0, 1'b1
endmodule
