// Logisim project 1805117.circ as structural Verilog: 1 circuit, main circuit main
module main (
  output Y0,
  output Y1
);

  wire button_1_out, clock_1_out, n7476_1_p3, n7476_1_p9;

  Clock clock_1 (.out(clock_1_out));
  Button button_1 (.out(button_1_out));
  // _7476 7476_1: pin names not known; wires that end beside it: clock_1_out, button_1_out, n7476_1_p3, 1'b1, clock_1_out, button_1_out, Y1, Y0, n7476_1_p9, 1'b0, n7476_1_p9, Y1, n7476_1_p3, Y0
endmodule
