// Logisim project 1805117.circ as structural Verilog: 1 circuit, main circuit main
module main (
  input  x1,
  input  x2,
  output Y1,
  output Y2,
  output Y3,
  output Z
);

  wire n7404_1_p2, n7404_1_p4, n7404_1_p6, n7404_1_p8, n7408_1_p3, n7408_1_p9, n7408_1_p12, n7408_2_p3,
       n7408_2_p9, n7408_3_p3, n7408_3_p9, n7408_4_p3, n7432_1_p1, n7432_1_p2, n7432_1_p3, n7432_1_p6,
       n7432_1_p8, n7432_1_p9, n7432_1_p11, n7432_1_p12;

  // _7404 7404_1: pin names not known; wires that end beside it: x2, n7404_1_p2, x1, n7404_1_p4, Y2, n7404_1_p6, Y1, n7404_1_p8
  // _7408 7408_1: pin names not known; wires that end beside it: Y1, n7404_1_p6, n7408_1_p3, n7408_1_p3, n7404_1_p2, Z, Y3, n7404_1_p4, n7408_1_p9, n7408_1_p9, x2, n7408_1_p12
  // _7432 7432_1: pin names not known; wires that end beside it: n7432_1_p1, n7432_1_p2, n7432_1_p3, n7432_1_p3, 1'b0, n7432_1_p6, n7408_1_p12, n7432_1_p8, n7432_1_p9, n7432_1_p9, n7432_1_p11, n7432_1_p12
  // _74116 74116_1: pin names not known; wires that end beside it: 1'b0, 1'b0, n7432_1_p12, Y1, n7432_1_p6, Y2, Y3
  // _7408 7408_2: pin names not known; wires that end beside it: n7404_1_p8, Y3, n7408_2_p3, n7408_2_p3, n7404_1_p4, n7432_1_p1, n7404_1_p6, Y3, n7408_2_p9, n7408_2_p9, n7404_1_p2, n7432_1_p2
  // _7408 7408_3: pin names not known; wires that end beside it: Y1, x1, n7408_3_p3, n7408_3_p3, n7404_1_p2, n7432_1_p8, Y1, Y2, n7408_3_p9, n7408_3_p9, n7404_1_p2, n7432_1_p11
  // _7408 7408_4: pin names not known; wires that end beside it: Y3, n7404_1_p4, n7408_4_p3, n7408_4_p3, x2, 1'b0
endmodule
